# Fritzing sketch schema (saved by Fritzing 1.0.4)
# 18650 Li-ion Battery: CC-BY Dr Kristofer Chan, King's College London/Remote-research.org

parts:
  part = j5019 [part_number=J5019]
  part_2 = Esp32-c3 super mini [part_number=ESP32-C3]
  part_3 = Rectifier Diode [part_number=1N4007 package="300 mil [THT]"]
  part_4 = Electrolytic Capacitor [capacitance=47nF voltage=6.3V package="100 mil [THT, electrolytic]"]
  part_5 = TTP223B Capacitive Touch Sensor Module [part_number=TTP223]
  part_6 = WS2812 RGB LED strip [part_number="WS2812B (10+3+3+3+3+3+3+3+3)"]
  part_7 = Resistor [tolerance=±5% power=0.5W resistance=330 package=THT]
  part_8 = Resistor [tolerance=±5% power=0.5W resistance=10k package=THT]
  GL5506 = Photocell (LDR) [power=0.25W dark_resistance_@0.01lx=300kΩ light_resistance_@100lx=400Ω luminance=10lx package=THT]
  BAT1 = 18650 Li-ion Battery [package=battery-18650]
  5V = Multimeter straight red probe  # not connected
  ON/OFF = Toggle Switch [package=THT]

nets:
  N1: part.Pin_1, part_3.anode
  GND: part.Pin_2, part.Pin_5, part_2.Pin_15, part_4.-, part_5.GND, part_6.GND, part_8.Pin_1, BAT1.-
  N2: part.Pin_6, ON/OFF.COM
  N3: part_2.Pin_9, GL5506.pin_1
  N4: part_2.Pin_10, part_8.Pin_0, GL5506.pin_0
  N5: part_2.Pin_12, part_7.Pin_0
  N6: part_2.Pin_13, part_5.SIG
  N7: part_2.Pin_14, part_5.VCC
  N8: part_2.Pin_16, part_3.cathode, part_4.+, part_6.VCC
  N9: part_6.DIN, part_7.Pin_1
  N10: BAT1.+, ON/OFF.L2

custom parts:
  j5019: This module is a small single cell lithium battery charging module which also includes a 1A step-up (boost) converter for powering a large range of applications.
  Esp32-c3 super mini: ESP32-C3 Development Board ESP32 SuperMini Development Board ESP32 Development Board WiFi Bluetooth.
  TTP223B Capacitive Touch Sensor Module: The TTP223B capacitive touch sensor module uses the TTP223B IC. The appropriate voltage is approximately 2 to 5.5 volts.
  WS2812 RGB LED strip: WS2812 strip
  18650 Li-ion Battery: 18650 li-ion Battery Standard 18650 battery with interactive connectors Creative Common Attribution 4.0 International (CC-BY 4.0) license. Any use of this part requires attribution of Dr Kristofer Chan, Department of Geography, King's College London. Contact kristofer.chan [at] kcl.ac.uk OR kris [at] remote-research.org for further information.
